# Fritzing sketch motor (saved by Fritzing 0.7.9b)
breadboards: 1

parts:
  Arduino1 = Arduino
  D1 = Rectifier Diode [part_number=1N4001 package="300 mil [THT]"]
  Q1 = NPN-Transistor [package="TO92 [THT]"]
  M1 = DC Motor

nets:
  N1: Arduino1.D9, Q1.B
  N2: Arduino1.+5V, D1.cathode, M1.pin_1
  N3: Arduino1.GND, Q1.E
  N4: D1.anode, Q1.C, M1.pin_2
